// Logisim project EMDS.circ as structural Verilog: 2 circuits, main circuit main
module main (
  input  [6:0] in_1,
  input  [6:0] in_2
);

  wire clock_1_out, clock_2_out, keyboard_1_avail, keyboard_2_avail, messenger_1_display_clock,
       messenger_1_incoming_monitor_clock, messenger_1_no_input_2, messenger_1_outgoing_message,
       messenger_1_output_command, messenger_2_display_clock, messenger_2_incoming_monitor_clock,
       messenger_2_no_input_2, messenger_2_outgoing_message, messenger_2_output_command;
  wire [6:0] keyboard_1_data, keyboard_2_data, messenger_1_incoming_monitor, messenger_1_outgoing_monitor,
       messenger_2_incoming_monitor, messenger_2_outgoing_monitor;

  Clock clock_1 (.out(clock_1_out));
  TTY tty_1 (.data(messenger_1_incoming_monitor), .clk(messenger_1_incoming_monitor_clock));  // open: we, clr
  TTY tty_2 (.data(messenger_1_outgoing_monitor), .clk(messenger_1_display_clock));  // open: we, clr
  Keyboard keyboard_1 (
    .clk(messenger_1_display_clock), .avail(keyboard_1_avail), .data(keyboard_1_data));  // open: re, clr
  Messenger messenger_1 (
    .Clock(clock_1_out), .Key(in_1), .Enable(1'b1), .Outgoing_message(messenger_1_outgoing_message),
    .Output_command(messenger_1_output_command), .Output_Clock(messenger_2_output_command),
    .Incoming_Message(messenger_2_outgoing_message),
    .Incoming_Monitor_Clock(messenger_1_incoming_monitor_clock),
    .Incoming_Monitor(messenger_1_incoming_monitor), .Display_CLock(messenger_1_display_clock),
    .Keyboard_IA(keyboard_1_avail), .Keyboard_Input(keyboard_1_data),
    .Outgoing_Monitor(messenger_1_outgoing_monitor), .No_INput_2(messenger_1_no_input_2),
    .No_Input(messenger_2_no_input_2));
  TTY tty_3 (.data(messenger_2_incoming_monitor), .clk(messenger_2_incoming_monitor_clock));  // open: we, clr
  Clock clock_2 (.out(clock_2_out));
  TTY tty_4 (.data(messenger_2_outgoing_monitor), .clk(messenger_2_display_clock));  // open: we, clr
  Keyboard keyboard_2 (
    .clk(messenger_2_display_clock), .avail(keyboard_2_avail), .data(keyboard_2_data));  // open: re, clr
  Messenger messenger_2 (
    .Clock(clock_2_out), .Key(in_2), .Enable(1'b1), .Outgoing_message(messenger_2_outgoing_message),
    .Output_command(messenger_2_output_command), .Output_Clock(messenger_1_output_command),
    .Incoming_Message(messenger_1_outgoing_message),
    .Incoming_Monitor_Clock(messenger_2_incoming_monitor_clock),
    .Incoming_Monitor(messenger_2_incoming_monitor), .Display_CLock(messenger_2_display_clock),
    .Keyboard_IA(keyboard_2_avail), .Keyboard_Input(keyboard_2_data),
    .Outgoing_Monitor(messenger_2_outgoing_monitor), .No_INput_2(messenger_2_no_input_2),
    .No_Input(messenger_1_no_input_2));
endmodule

module Messenger (
  input  Keyboard_IA,
  input  [6:0] Keyboard_Input,
  input  Clock,
  input  [6:0] Key,
  input  Enable,
  input  Output_Clock,
  input  Incoming_Message,
  input  No_Input,
  output Incoming_Monitor_Clock,
  output [6:0] Incoming_Monitor,
  output Display_CLock,
  output [6:0] Outgoing_Monitor,
  output No_INput_2,
  output Outgoing_message,
  output Output_command
);

  wire Encoder_clock_output;
  wire [6:0] Decrypter_p4, Encrypter_encrypted_message;

  // Decrypter Decrypter: pin names not known; wires that end beside it: Incoming_Monitor, No_Input, Key, Decrypter_p4
  assign Display_CLock = Keyboard_IA ? Encoder_clock_output : 1'bz;  // Controlled_Buffer controlled_buffer_1
  Encrypter Encrypter (
    .Input_7bit_Ascii(Keyboard_Input), .Private_Key_Input(Key),
    .Encrypted_Message(Encrypter_encrypted_message), .No_Input(No_INput_2));
  Encoder Encoder (
    .Clock(Clock), .Enable(Enable), .Output(Outgoing_message), .Input_Available(Keyboard_IA),
    .Clock_Output(Encoder_clock_output), .op_when(Output_command), .ASCII_Data(Encrypter_encrypted_message));
  Decoder Decoder (
    .CLOCK(Clock), .SerialIn(Incoming_Message), .Enable(Enable), .OP_CLOCK(Output_Clock),
    .ASCII(Decrypter_p4), .OP_CLOCK_2(Incoming_Monitor_Clock));

  assign Outgoing_Monitor = Keyboard_Input;
endmodule
